# Fritzing sketch Fritzing Schematic (saved by Fritzing 0.9.3b)
breadboards: 1

parts:
  Raspberry_Pi_1 = Raspberry Pi 3 [part_number=RPI-3-V1.2]
  J1 = Active Buzzer
  S1 = Push Button [package="[THT]"]
  Q1 = NPN-Transistor [package="SOT-23 [SMD]"]
  R1 = Resistor [tolerance=±5% resistance=1k package=THT]

nets:
  3V3: Raspberry_Pi_1.3v3, Raspberry_Pi_1.3V3, S1.Pin_3, S1.Pin_4
  N1: Raspberry_Pi_1.GIPO21, R1.Pin_1
  N2: Raspberry_Pi_1.GIPO20, S1.Pin_1, S1.Pin_2
  N3: Raspberry_Pi_1.GND, Q1.2
  N4: Raspberry_Pi_1.5V, J1.pin2
  N5: J1.pin1, Q1.1
  N6: Q1.0, R1.Pin_0

custom parts:
  Active Buzzer: Piezo
  Push Button: A generic pushbutton.
