# Fritzing sketch Fritzing Schematic (saved by Fritzing 0.9.6b)
breadboards: 1

parts:
  Raspberry_Pi_1 = Raspberry Pi 3 [part_number=RPI-3-V1.2]
  J1 = Active Buzzer
  Q1 = NPN-Transistor [package="SOT-23 [SMD]"]
  R2 = 1kΩ Resistor [package=THT]
  S1 = Push Button [package="[THT]"]

nets:
  N1: Raspberry_Pi_1.GPIO21, R2.Pin_1
  N2: Raspberry_Pi_1.GPIO20, S1.Pin_1, S1.Pin_2
  N3: Raspberry_Pi_1.GND, Q1.2, S1.Pin_3, S1.Pin_4
  N4: Raspberry_Pi_1.5V, J1.pin2
  N5: J1.pin1, Q1.1
  N6: Q1.0, R2.Pin_0

custom parts:
  Active Buzzer: Piezo
  1kΩ Resistor: A generic 5-band resistor (0.25W)
  Push Button: A generic pushbutton.
