# Fritzing sketch Fritzing Schematic (saved by Fritzing 0.9.6b)
breadboards: 1

parts:
  Raspberry_Pi_1 = Raspberry Pi 3 [part_number=RPI-3-V1.2]
  LED1 = LED - 3mm [color="Red (633nm)" current=0.030 package="3 mm [THT]"]
  S1 = Push Button [package="[THT]"]
  R1 = Resistor [tolerance=±5% power=0.25 resistance=220 package=THT]

nets:
  N1: Raspberry_Pi_1.3v3, LED1.anode
  N2: Raspberry_Pi_1.GPIO21, R1.Pin_1
  N3: Raspberry_Pi_1.GPIO20, S1.Pin_3, S1.Pin_4
  N4: Raspberry_Pi_1.GND, S1.Pin_1, S1.Pin_2
  N5: LED1.cathode, R1.Pin_0

custom parts:
  Push Button: A generic pushbutton.
