# Fritzing sketch Fritzing Schematic (saved by Fritzing 0.9.3b)
breadboards: 1

parts:
  Raspberry_Pi_1 = Raspberry Pi 3 [part_number=RPI-3-V1.2]
  D1 = LED_BARGRAPH_10 [package=led_bargaph_10]
  R1 = Resistor [tolerance=±5% resistance=220 package=THT]
  R3 = Resistor [tolerance=±5% resistance=220 package=THT]
  R4 = Resistor [tolerance=±5% resistance=220 package=THT]
  R5 = Resistor [tolerance=±5% resistance=220 package=THT]
  R6 = Resistor [tolerance=±5% resistance=220 package=THT]
  R7 = Resistor [tolerance=±5% resistance=220 package=THT]
  R8 = Resistor [tolerance=±5% resistance=220 package=THT]
  R9 = Resistor [tolerance=±5% resistance=220 package=THT]
  R10 = Resistor [tolerance=±5% resistance=220 package=THT]
  R12 = Resistor [tolerance=±5% resistance=220 package=THT]

nets:
  N1: Raspberry_Pi_1.3v3, R1.Pin_0, R3.Pin_0, R4.Pin_0, R5.Pin_0, R6.Pin_0, R7.Pin_0, R8.Pin_0, R9.Pin_0, R10.Pin_0, R12.Pin_0
  N2: Raspberry_Pi_1.GIPO21, D1.A_C
  N3: Raspberry_Pi_1.GIPO20, D1.B_C
  N4: Raspberry_Pi_1.GIPO16, D1.C_C
  N5: Raspberry_Pi_1.GIPO12, D1.D_C
  N6: Raspberry_Pi_1.GIPO7, D1.E_C
  N7: Raspberry_Pi_1.GIPO8, D1.F_C
  N8: Raspberry_Pi_1.GIPO25, D1.G_C
  N9: Raspberry_Pi_1.GIPO24, D1.H_C
  N10: Raspberry_Pi_1.GIPO23, D1.I_C
  N11: Raspberry_Pi_1.GIPO18, D1.J_C
  N12: D1.A_A, R1.Pin_1
  N13: D1.B_A, R6.Pin_1
  N14: D1.C_A, R5.Pin_1
  N15: D1.D_A, R4.Pin_1
  N16: D1.E_A, R12.Pin_1
  N17: D1.F_A, R3.Pin_1
  N18: D1.G_A, R7.Pin_1
  N19: D1.H_A, R10.Pin_1
  N20: D1.I_A, R9.Pin_1
  N21: D1.J_A, R8.Pin_1
