# Fritzing sketch Fritzing Schematic (saved by Fritzing 0.9.3b)
breadboards: 1

parts:
  Raspberry_Pi_1 = Raspberry Pi 3 [part_number=RPI-3-V1.2]
  LED1 = LED - 3mm [color="Red (633nm)" package="3 mm [THT]"]
  R1 = Resistor [tolerance=±5% resistance=220 package=THT]
  S1 = Push Button [package="[THT]"]

nets:
  3V3: Raspberry_Pi_1.3v3, Raspberry_Pi_1.3V3, Raspberry_Pi_1.GIPO20, S1.Pin_3, S1.Pin_4
  N1: Raspberry_Pi_1.GIPO21, R1.Pin_0
  N2: LED1.cathode, R1.Pin_1
  N3: S1.Pin_1, S1.Pin_2

custom parts:
  Push Button: A generic pushbutton.
