# Fritzing sketch Fritzing Schematic (saved by Fritzing 0.9.3b)
breadboards: 1

parts:
  Raspberry_Pi_1 = Raspberry Pi 3 [part_number=RPI-3-V1.2]
  LED1 = RGB LED - (4 legs) [package="5 mm [THT]"]
  R1 = Resistor [tolerance=±5% resistance=220 package=THT]
  R2 = Resistor [tolerance=±5% resistance=220 package=THT]
  R3 = Resistor [tolerance=±5% resistance=220 package=THT]

nets:
  N1: Raspberry_Pi_1.3v3, LED1.common_anode
  N2: Raspberry_Pi_1.GIPO21, R1.Pin_0
  N3: Raspberry_Pi_1.GIPO20, R2.Pin_0
  N4: Raspberry_Pi_1.GIPO16, R3.Pin_0
  N5: LED1.red_cathode, R1.Pin_1
  N6: LED1.green_cathode, R2.Pin_1
  N7: LED1.blue_cathode, R3.Pin_1
